// Digital circuit labtimer.dig as structural Verilog
module labtimer (
  input  CLK,
  input  SW,
  input  B3,
  input  B2,
  input  B1,
  input  B0,
  input  HZ1,
  output [3:0] M10,
  output [3:0] M1,
  output [3:0] S10,
  output [3:0] S1
);

  wire A_2_nq, A_2_q, A_3_nq, A_3_q, A_4_nq, A_4_q, A_5_nq, A_5_q, A_nq, A_q, and_1_out, and_2_out,
       and_3_out, and_4_out, and_5_out, and_6_out, and_7_out, and_8_out, and_9_out, and_10_out, and_11_out,
       and_12_out, and_13_out, and_14_out, and_15_out, and_16_out, and_17_out, and_18_out, and_19_out,
       and_20_out, and_21_out, and_22_out, and_35_out, and_36_out, and_37_out, and_38_out, and_39_out,
       and_40_out, and_41_out, and_42_out, and_43_out, and_44_out, and_45_out, and_46_out, and_47_out,
       B_2_nq, B_2_q, B_3_nq, B_3_q, B_4_nq, B_4_q, B_5_nq, B_5_q, B_nq, B_q, d_ff_1_nq, d_ff_2_nq,
       d_ff_3_nq, d_ff_4_nq, d_ff_5_nq, d_ff_6_nq, d_ff_7_nq, d_ff_8_nq, d_ff_9_nq, d_ff_10_nq, d_ff_11_nq,
       d_ff_12_nq, d_ff_13_nq, d_ff_14_nq, d_ff_15_nq, d_ff_16_nq, d_ff_17_q, demultiplexer_1_out_0,
       demultiplexer_1_out_1, multiplexer_1_out, multiplexer_2_out, multiplexer_3_out, multiplexer_4_out,
       multiplexer_5_out, multiplexer_6_out, multiplexer_7_out, multiplexer_8_out, multiplexer_9_out,
       multiplexer_10_out, multiplexer_11_out, multiplexer_12_out, multiplexer_13_out, multiplexer_14_out,
       multiplexer_15_out, multiplexer_16_out, multiplexer_17_out, multiplexer_18_out, multiplexer_19_out,
       multiplexer_20_out, multiplexer_21_out, multiplexer_22_out, multiplexer_23_out, multiplexer_24_out,
       multiplexer_25_out, multiplexer_26_out, multiplexer_27_out, multiplexer_28_out, nand_1_out,
       nand_2_out, nand_3_out, not_1_out, not_2_out, not_3_out, not_4_out, not_5_out, not_6_out, not_7_out,
       not_8_out, not_9_out, not_10_out, not_11_out, not_12_out, not_13_out, not_14_out, not_15_out,
       not_16_out, not_17_out, not_18_out, not_19_out, not_20_out, not_21_out, not_22_out, not_23_out,
       not_24_out, not_25_out, not_26_out, not_27_out, not_28_out, not_29_out, not_30_out, not_31_out,
       not_32_out, not_33_out, not_34_out, not_35_out, not_36_out, or_1_out, or_2_out, or_3_out, or_4_out,
       or_9_out, xor_1_out, xor_2_out, xor_3_out, xor_4_out, xor_5_out;
  wire [0:0] and_23_out, and_25_out, and_27_out, and_28_out, and_30_out, and_31_out, and_32_out, and_33_out,
       and_34_out, xor_6_out, xor_7_out, xor_8_out;
  wire [1:0] or_5_out, or_6_out, or_7_out, or_8_out;

  not not_1 (not_1_out, B3);
  not not_2 (not_2_out, B2);
  not not_3 (not_3_out, B1);
  not not_4 (not_4_out, B0);
  and and_1 (and_1_out, SW, not_1_out);
  and and_2 (and_2_out, SW, not_2_out);
  and and_3 (and_3_out, SW, not_3_out);
  and and_4 (and_4_out, SW, not_4_out);
  not not_5 (not_5_out, SW);
  and and_5 (and_5_out, not_5_out, HZ1);
  xor xor_1 (xor_1_out, A_q, B_q);
  xor xor_2 (xor_2_out, A_2_q, B_2_q);
  xor xor_3 (xor_3_out, A_3_q, B_3_q);
  xor xor_4 (xor_4_out, A_4_q, B_4_q);
  xor xor_5 (xor_5_out, A_5_q, B_5_q);
  and and_6 (and_6_out, xor_1_out, and_1_out);
  and and_7 (and_7_out, A_nq, and_1_out, B_nq);
  and and_8 (and_8_out, xor_2_out, and_2_out);
  and and_9 (and_9_out, A_2_nq, and_2_out, B_2_nq);
  and and_10 (and_10_out, xor_3_out, and_3_out);
  and and_11 (and_11_out, A_3_nq, and_3_out, B_3_nq);
  and and_12 (and_12_out, xor_4_out, and_4_out);
  and and_13 (and_13_out, A_4_nq, and_4_out, B_4_nq);
  and and_14 (and_14_out, xor_5_out, and_5_out);
  and and_15 (and_15_out, A_5_nq, and_5_out, B_5_nq);
  D_FF A (.D(and_6_out), .C(CLK), .Q(A_q), .nQ(A_nq));
  D_FF B (.D(and_7_out), .C(CLK), .Q(B_q), .nQ(B_nq));
  D_FF A_2 (.D(and_8_out), .C(CLK), .Q(A_2_q), .nQ(A_2_nq));
  D_FF B_2 (.D(and_9_out), .C(CLK), .Q(B_2_q), .nQ(B_2_nq));
  D_FF A_3 (.D(and_10_out), .C(CLK), .Q(A_3_q), .nQ(A_3_nq));
  D_FF B_3 (.D(and_11_out), .C(CLK), .Q(B_3_q), .nQ(B_3_nq));
  D_FF A_4 (.D(and_12_out), .C(CLK), .Q(A_4_q), .nQ(A_4_nq));
  D_FF B_4 (.D(and_13_out), .C(CLK), .Q(B_4_q), .nQ(B_4_nq));
  D_FF A_5 (.D(and_14_out), .C(CLK), .Q(A_5_q), .nQ(A_5_nq));
  D_FF B_5 (.D(and_15_out), .C(CLK), .Q(B_5_q), .nQ(B_5_nq));
  Demultiplexer demultiplexer_1 (
    .sel(d_ff_17_q), .in(and_15_out), .out_0(demultiplexer_1_out_0), .out_1(demultiplexer_1_out_1));
  or or_1 (or_1_out, and_13_out, demultiplexer_1_out_1);
  and and_16 (and_16_out, demultiplexer_1_out_1, and_45_out, and_44_out, and_43_out);
  and and_17 (and_17_out, demultiplexer_1_out_1, and_44_out, and_45_out);
  and and_18 (and_18_out, demultiplexer_1_out_1, and_45_out);
  or or_2 (or_2_out, and_7_out, and_16_out);
  or or_3 (or_3_out, and_9_out, and_17_out);
  or or_4 (or_4_out, and_11_out, and_18_out);
  not not_6 (not_6_out, and_35_out);
  nand nand_1 (nand_1_out, and_35_out, and_36_out);
  nand nand_2 (nand_2_out, and_35_out, and_36_out, and_37_out);
  nand nand_3 (nand_3_out, and_35_out, and_36_out, and_37_out, and_38_out);
  and and_19 (and_19_out, demultiplexer_1_out_0, and_38_out, and_37_out, and_36_out, not_6_out);
  and and_20 (and_20_out, demultiplexer_1_out_0, nand_1_out, and_37_out, and_38_out);
  and and_21 (and_21_out, demultiplexer_1_out_0, nand_2_out, and_38_out);
  and and_22 (and_22_out, demultiplexer_1_out_0, nand_3_out);
  xor xor_6 (xor_6_out[0], or_2_out, and_19_out);
  xor xor_7 (xor_7_out[0], or_3_out, and_20_out);
  xor xor_8 (xor_8_out[0], or_4_out, and_21_out);
  xor xor_9 (or_8_out[0], or_1_out, and_22_out);
  and and_23 (and_23_out[0], multiplexer_17_out, xor_6_out[0]);
  and and_24 (or_5_out[0], multiplexer_18_out, and_23_out[0]);
  and and_25 (and_25_out[0], multiplexer_19_out, or_5_out[0]);
  and and_26 (or_6_out[0], multiplexer_20_out, xor_7_out[0]);
  and and_27 (and_27_out[0], multiplexer_21_out, or_6_out[0]);
  and and_28 (and_28_out[0], multiplexer_22_out, and_27_out[0]);
  and and_29 (or_7_out[0], multiplexer_23_out, xor_8_out[0]);
  and and_30 (and_30_out[0], multiplexer_24_out, or_7_out[0]);
  and and_31 (and_31_out[0], multiplexer_25_out, and_30_out[0]);
  and and_32 (and_32_out[0], multiplexer_26_out, or_8_out[0]);
  and and_33 (and_33_out[0], multiplexer_27_out, and_32_out[0]);
  and and_34 (and_34_out[0], multiplexer_28_out, and_33_out[0]);
  Multiplexer #(.Selector_Bits(2)) multiplexer_1 (
    .sel({or_5_out[1], xor_6_out[0]}), .in_0(M10[0]), .in_1(d_ff_1_nq), .in_2(1'b0), .in_3(1'b1),
    .out(multiplexer_1_out));
  Multiplexer #(.Selector_Bits(2)) multiplexer_2 (
    .sel({or_5_out[1], and_23_out[0]}), .in_0(M10[1]), .in_1(d_ff_2_nq), .in_2(1'b0), .in_3(1'b0),
    .out(multiplexer_2_out));
  Multiplexer #(.Selector_Bits(2)) multiplexer_3 (
    .sel(or_5_out), .in_0(M10[2]), .in_1(d_ff_3_nq), .in_2(1'b0), .in_3(1'b0), .out(multiplexer_3_out));
  Multiplexer #(.Selector_Bits(2)) multiplexer_4 (
    .sel({or_5_out[1], and_25_out[0]}), .in_0(M10[3]), .in_1(d_ff_4_nq), .in_2(1'b0), .in_3(1'b1),
    .out(multiplexer_4_out));
  Multiplexer #(.Selector_Bits(2)) multiplexer_5 (
    .sel({or_6_out[1], xor_7_out[0]}), .in_0(M1[0]), .in_1(d_ff_5_nq), .in_2(1'b0), .in_3(1'b1),
    .out(multiplexer_5_out));
  Multiplexer #(.Selector_Bits(2)) multiplexer_6 (
    .sel(or_6_out), .in_0(M1[1]), .in_1(d_ff_6_nq), .in_2(1'b0), .in_3(1'b0), .out(multiplexer_6_out));
  Multiplexer #(.Selector_Bits(2)) multiplexer_7 (
    .sel({or_6_out[1], and_27_out[0]}), .in_0(M1[2]), .in_1(d_ff_7_nq), .in_2(1'b0), .in_3(1'b0),
    .out(multiplexer_7_out));
  Multiplexer #(.Selector_Bits(2)) multiplexer_8 (
    .sel({or_6_out[1], and_28_out[0]}), .in_0(M1[3]), .in_1(d_ff_8_nq), .in_2(1'b0), .in_3(1'b1),
    .out(multiplexer_8_out));
  Multiplexer #(.Selector_Bits(2)) multiplexer_9 (
    .sel({or_7_out[1], xor_8_out[0]}), .in_0(S10[0]), .in_1(d_ff_9_nq), .in_2(1'b0), .in_3(1'b1),
    .out(multiplexer_9_out));
  Multiplexer #(.Selector_Bits(2)) multiplexer_10 (
    .sel(or_7_out), .in_0(S10[1]), .in_1(d_ff_10_nq), .in_2(1'b0), .in_3(1'b0), .out(multiplexer_10_out));
  Multiplexer #(.Selector_Bits(2)) multiplexer_11 (
    .sel({or_7_out[1], and_30_out[0]}), .in_0(S10[2]), .in_1(d_ff_11_nq), .in_2(1'b0), .in_3(1'b1),
    .out(multiplexer_11_out));
  Multiplexer #(.Selector_Bits(2)) multiplexer_12 (
    .sel({or_7_out[1], and_31_out[0]}), .in_0(S10[3]), .in_1(d_ff_12_nq), .in_2(1'b0), .in_3(1'b0),
    .out(multiplexer_12_out));
  Multiplexer #(.Selector_Bits(2)) multiplexer_13 (
    .sel(or_8_out), .in_0(S1[0]), .in_1(d_ff_13_nq), .in_2(1'b0), .in_3(1'b1), .out(multiplexer_13_out));
  Multiplexer #(.Selector_Bits(2)) multiplexer_14 (
    .sel({or_8_out[1], and_32_out[0]}), .in_0(S1[1]), .in_1(d_ff_14_nq), .in_2(1'b0), .in_3(1'b0),
    .out(multiplexer_14_out));
  Multiplexer #(.Selector_Bits(2)) multiplexer_15 (
    .sel({or_8_out[1], and_33_out[0]}), .in_0(S1[2]), .in_1(d_ff_15_nq), .in_2(1'b0), .in_3(1'b0),
    .out(multiplexer_15_out));
  Multiplexer #(.Selector_Bits(2)) multiplexer_16 (
    .sel({or_8_out[1], and_34_out[0]}), .in_0(S1[3]), .in_1(d_ff_16_nq), .in_2(1'b0), .in_3(1'b1),
    .out(multiplexer_16_out));
  D_FF d_ff_1 (.D(multiplexer_1_out), .C(CLK), .Q(M10[0]), .nQ(d_ff_1_nq));
  D_FF d_ff_2 (.D(multiplexer_2_out), .C(CLK), .Q(M10[1]), .nQ(d_ff_2_nq));
  D_FF d_ff_3 (.D(multiplexer_3_out), .C(CLK), .Q(M10[2]), .nQ(d_ff_3_nq));
  D_FF d_ff_4 (.D(multiplexer_4_out), .C(CLK), .Q(M10[3]), .nQ(d_ff_4_nq));
  D_FF d_ff_5 (.D(multiplexer_5_out), .C(CLK), .Q(M1[0]), .nQ(d_ff_5_nq));
  D_FF d_ff_6 (.D(multiplexer_6_out), .C(CLK), .Q(M1[1]), .nQ(d_ff_6_nq));
  D_FF d_ff_7 (.D(multiplexer_7_out), .C(CLK), .Q(M1[2]), .nQ(d_ff_7_nq));
  D_FF d_ff_8 (.D(multiplexer_8_out), .C(CLK), .Q(M1[3]), .nQ(d_ff_8_nq));
  D_FF d_ff_9 (.D(multiplexer_9_out), .C(CLK), .Q(S10[0]), .nQ(d_ff_9_nq));
  D_FF d_ff_10 (.D(multiplexer_10_out), .C(CLK), .Q(S10[1]), .nQ(d_ff_10_nq));
  D_FF d_ff_11 (.D(multiplexer_11_out), .C(CLK), .Q(S10[2]), .nQ(d_ff_11_nq));
  D_FF d_ff_12 (.D(multiplexer_12_out), .C(CLK), .Q(S10[3]), .nQ(d_ff_12_nq));
  D_FF d_ff_13 (.D(multiplexer_13_out), .C(CLK), .Q(S1[0]), .nQ(d_ff_13_nq));
  D_FF d_ff_14 (.D(multiplexer_14_out), .C(CLK), .Q(S1[1]), .nQ(d_ff_14_nq));
  D_FF d_ff_15 (.D(multiplexer_15_out), .C(CLK), .Q(S1[2]), .nQ(d_ff_15_nq));
  D_FF d_ff_16 (.D(multiplexer_16_out), .C(CLK), .Q(S1[3]), .nQ(d_ff_16_nq));
  Multiplexer multiplexer_17 (.sel(or_2_out), .in_0(d_ff_1_nq), .in_1(M10[0]), .out(multiplexer_17_out));
  Multiplexer multiplexer_18 (.sel(or_2_out), .in_0(d_ff_2_nq), .in_1(M10[1]), .out(multiplexer_18_out));
  Multiplexer multiplexer_19 (.sel(or_2_out), .in_0(d_ff_3_nq), .in_1(M10[2]), .out(multiplexer_19_out));
  Multiplexer multiplexer_20 (.sel(or_3_out), .in_0(d_ff_5_nq), .in_1(M1[0]), .out(multiplexer_20_out));
  Multiplexer multiplexer_21 (.sel(or_3_out), .in_0(d_ff_6_nq), .in_1(M1[1]), .out(multiplexer_21_out));
  Multiplexer multiplexer_22 (.sel(or_3_out), .in_0(d_ff_7_nq), .in_1(M1[2]), .out(multiplexer_22_out));
  Multiplexer multiplexer_23 (.sel(or_4_out), .in_0(d_ff_9_nq), .in_1(S10[0]), .out(multiplexer_23_out));
  Multiplexer multiplexer_24 (.sel(or_4_out), .in_0(d_ff_10_nq), .in_1(S10[1]), .out(multiplexer_24_out));
  Multiplexer multiplexer_25 (.sel(or_4_out), .in_0(d_ff_11_nq), .in_1(S10[2]), .out(multiplexer_25_out));
  Multiplexer multiplexer_26 (.sel(or_1_out), .in_0(d_ff_13_nq), .in_1(S1[0]), .out(multiplexer_26_out));
  Multiplexer multiplexer_27 (.sel(or_1_out), .in_0(d_ff_14_nq), .in_1(S1[1]), .out(multiplexer_27_out));
  Multiplexer multiplexer_28 (.sel(or_1_out), .in_0(d_ff_15_nq), .in_1(S1[2]), .out(multiplexer_28_out));
  not not_7 (not_7_out, M10[3]);
  not not_8 (not_8_out, M10[2]);
  not not_9 (not_9_out, M1[3]);
  not not_10 (not_10_out, M1[2]);
  not not_11 (not_11_out, S10[3]);
  not not_12 (not_12_out, S10[2]);
  not not_13 (not_13_out, S1[3]);
  not not_14 (not_14_out, S1[2]);
  not not_15 (not_15_out, M10[1]);
  not not_16 (not_16_out, M10[0]);
  and and_35 (and_35_out, not_16_out, not_15_out, not_8_out, not_7_out);
  not not_17 (not_17_out, M1[1]);
  not not_18 (not_18_out, M1[0]);
  and and_36 (and_36_out, not_18_out, not_17_out, not_10_out, not_9_out);
  not not_19 (not_19_out, S10[1]);
  not not_20 (not_20_out, S10[0]);
  and and_37 (and_37_out, not_20_out, not_19_out, not_12_out, not_11_out);
  not not_21 (not_21_out, S1[1]);
  not not_22 (not_22_out, S1[0]);
  and and_38 (and_38_out, not_22_out, not_21_out, not_14_out, not_13_out);
  not not_23 (not_23_out, M10[2]);
  or or_5 (or_5_out[1], and_39_out, and_35_out);
  not not_24 (not_24_out, M1[2]);
  or or_6 (or_6_out[1], and_40_out, and_36_out);
  not not_25 (not_25_out, S10[3]);
  or or_7 (or_7_out[1], and_41_out, and_37_out);
  not not_26 (not_26_out, S1[2]);
  or or_8 (or_8_out[1], and_42_out, and_38_out);
  not not_27 (not_27_out, M10[0]);
  and and_39 (and_39_out, not_27_out, M10[1], not_23_out, M10[3]);
  not not_28 (not_28_out, M1[0]);
  not not_29 (not_29_out, M1[2]);
  and and_40 (and_40_out, not_28_out, M1[1], not_24_out, M1[3]);
  not not_30 (not_30_out, S10[0]);
  not not_31 (not_31_out, S10[3]);
  and and_41 (and_41_out, not_30_out, S10[1], S10[2], not_25_out);
  not not_32 (not_32_out, S1[0]);
  not not_33 (not_33_out, S1[2]);
  and and_42 (and_42_out, not_32_out, S1[1], not_26_out, S1[3]);
  not not_34 (not_34_out, M1[1]);
  and and_43 (and_43_out, M1[0], not_34_out, not_29_out, M1[3]);
  not not_35 (not_35_out, S10[1]);
  and and_44 (and_44_out, S10[0], not_35_out, S10[2], not_31_out);
  not not_36 (not_36_out, S1[1]);
  and and_45 (and_45_out, S1[0], not_36_out, not_33_out, S1[3]);
  and and_46 (and_46_out, and_35_out, and_36_out, and_37_out, and_38_out);
  or or_9 (or_9_out, d_ff_17_q, and_46_out);
  and and_47 (and_47_out, or_9_out, not_5_out);
  D_FF d_ff_17 (.D(and_47_out), .C(CLK), .Q(d_ff_17_q));  // open: nQ

  // Notes on the sheet:
  //   SW: default 1
endmodule
